// Logisim project alu.circ as structural Verilog: 1 circuit, main circuit alu
module alu (
  input  [31:0] A,
  input  [31:0] B,
  input  [3:0] ALUSel,
  output [31:0] Result
);

  wire [0:0] r2;
  wire [31:0] r0, r1, r4, r5, r6, r7, r8, r9, r11, r12, r13, r15, SELB;
  wire [63:0] add, AN_D, MU_L, MUL_H, MULH_U, O_R, ShiftL, ShiftR, SLS, SR_A, SUB, XO;

  Demultiplexer #(.enable("false"), .select(4), .width(64)) demultiplexer_1 (
    .out0(add), .out1(ShiftL), .out2(SLS), .out4(XO), .out5(ShiftR), .out6(O_R), .out7(AN_D), .out8(MU_L),
    .out9(MUL_H), .out11(MULH_U), .out12(SUB), .out13(SR_A), .out15({r15, SELB}), .in({B, A}), .sel(ALUSel));  // open: out3, out10, out14
  Adder #(.width(32)) adder_1 (.a(add[31:0]), .b(add[63:32]), .out(r0));  // open: cin, cout
  Shifter #(.width(32)) shifter_1 (.in(ShiftL[31:0]), .\dist (ShiftL[36:32]), .out(r1));
  Comparator #(.width(32)) comparator_1 (.a(SLS[31:0]), .b(SLS[63:32]), .lt(r2[0]));  // open: gt, eq
  assign r4 = XO[31:0] ^ XO[63:32];  // XOR_Gate xor_1, 32 bits wide
  Shifter #(.shift("lr"), .width(32)) shifter_2 (.in(ShiftR[31:0]), .\dist (ShiftR[36:32]), .out(r5));
  assign r6 = O_R[31:0] | O_R[63:32];  // OR_Gate or_1, 32 bits wide
  assign r7 = AN_D[31:0] & AN_D[63:32];  // AND_Gate and_1, 32 bits wide
  Multiplier #(.mode("twosComplement"), .width(32)) multiplier_1 (
    .a(MU_L[31:0]), .b(MU_L[63:32]), .out(r8));  // open: cin, cout
  Multiplier #(.mode("twosComplement"), .width(32)) multiplier_2 (
    .a(MUL_H[31:0]), .b(MUL_H[63:32]), .cout(r9));  // open: out, cin
  Multiplier #(.width(32)) multiplier_3 (.a(MULH_U[31:0]), .b(MULH_U[63:32]), .cout(r11));  // open: out, cin
  Subtractor #(.width(32)) subtractor_1 (.a(SUB[31:0]), .b(SUB[63:32]), .out(r12));  // open: bin, bout
  Shifter #(.shift("ar"), .width(32)) shifter_3 (.in(SR_A[31:0]), .\dist (SR_A[36:32]), .out(r13));
  Multiplexer #(.enable("false"), .select(4), .width(32)) multiplexer_1 (
    .in0(r0), .in1(r1), .in2({{31{1'b0}}, r2[0]}), .in3({32{1'b0}}), .in4(r4), .in5(r5), .in6(r6), .in7(r7),
    .in8(r8), .in9(r9), .in10({32{1'b0}}), .in11(r11), .in12(r12), .in13(r13), .in14({32{1'b0}}), .in15(r15),
    .out(Result), .sel(ALUSel));

  // Other names for the same wires on the sheet: A_t[63:0] = {B, A}; SELB[63:32] = r15

  // Notes on the sheet:
  //   INPUTS to circuit
  //   OUTPUT from circuit
endmodule
