// Logisim project control-logic.circ as structural Verilog: 1 circuit, main circuit control_logic
module control_logic (
  input  [31:0] inst,
  input  BrEq,
  input  BrLt,
  output PCSel,
  output RegWEn,
  output [2:0] ImmSel,
  output BrUn,
  output ASel,
  output BSel,
  output [3:0] ALUSel,
  output MemRW,
  output [1:0] WBSel,
  output CSRSel,
  output CSRWen
);

  wire and_1_out, and_2_out, and_3_out, not_1_out, not_2_out, or_3_out, or_4_out, xor_1_out, xor_2_out;
  wire [2:0] demultiplexer_2_out0, demultiplexer_2_out1;
  wire [5:0] CSR_R, I_R, multiplexer_7_out, multiplexer_8_out, multiplexer_9_out, multiplexer_10_out, R_R,
       Result, S_R, SB_R, U_R;
  wire [24:0] CSR, demultiplexer_1_out0, demultiplexer_1_out4, demultiplexer_1_out5, demultiplexer_1_out6,
       demultiplexer_1_out13, demultiplexer_1_out25, I, R, S, SB, U, UJ;

  Demultiplexer #(.enable("false"), .select(5), .width(25)) demultiplexer_1 (
    .out0(demultiplexer_1_out0), .out4(demultiplexer_1_out4), .out5(demultiplexer_1_out5),
    .out6(demultiplexer_1_out6), .out8(S), .out12(R), .out13(demultiplexer_1_out13), .out24(SB),
    .out25(demultiplexer_1_out25), .out27(UJ), .out28(CSR), .in(inst[31:7]), .sel(inst[6:2]));  // open: out1, out2, out3, out7, out9, out10, out11, out14, out15, out16, out17, out18, out19, out20, out21, out22, out23, out26, out29, out30, out31
  ROM #(.addrWidth(6), .dataWidth(16)) rom_1 (
    .addr(Result), .data({RegWEn, ImmSel, BrUn, ASel, BSel, ALUSel, MemRW, WBSel, CSRSel, CSRWen}));
  assign U = demultiplexer_1_out5 | demultiplexer_1_out13;  // OR_Gate or_1, 25 bits wide
  Multiplexer #(.enable("false"), .select(2), .width(6)) multiplexer_1 (
    .in0(6'b010111), .in1(6'b011000), .in2(6'b011001), .out(S_R), .sel(S[6:5]));  // open: in3
  Multiplexer #(.enable("false"), .select(3), .width(6)) multiplexer_2 (
    .in0(6'b011010), .in1(6'b011011), .in4(6'b011100), .in5(6'b011101), .in6(6'b011110), .in7(6'b011111),
    .out(SB_R), .sel(SB[7:5]));  // open: in2, in3
  Multiplexer #(.enable("false"), .width(6)) multiplexer_3 (.in0(6'b100000), .in1(6'b100001), .out(U_R), .sel(inst[5]));
  Multiplexer #(.enable("false"), .width(6)) multiplexer_4 (
    .in0(6'b100100), .in1(6'b100101), .out(CSR_R), .sel(CSR[7]));
  assign I = demultiplexer_1_out0 | demultiplexer_1_out4 | demultiplexer_1_out6 | demultiplexer_1_out25;  // OR_Gate or_2, 25 bits wide
  Multiplexer #(.enable("false"), .select(5), .width(6)) multiplexer_5 (
    .in0({6{1'b0}}), .in1(6'b000011), .in2(6'b000110), .in4(6'b000111), .in5(6'b001000), .in6(6'b001010),
    .in7(6'b001011), .in8(6'b000001), .in9(6'b000100), .in11(6'b000101), .in16(6'b000010), .in21(6'b001001),
    .out(R_R), .sel({R[23], R[18], R[7:5]}));  // open: in3, in10, in12, in13, in14, in15, in17, in18, in19, in20, in22, in23, in24, in25, in26, in27, in28, in29, in30, in31
  Demultiplexer #(.enable("false"), .width(3)) demultiplexer_2 (
    .out0(demultiplexer_2_out0), .out1(demultiplexer_2_out1), .in(I[7:5]), .sel(inst[4]));
  Multiplexer #(.enable("false"), .select(5), .width(6)) multiplexer_6 (
    .in0(I_R), .in4(I_R), .in5(U_R), .in6(I_R), .in8(S_R), .in12(R_R), .in13(U_R), .in24(SB_R), .in25(I_R),
    .in27(6'b100010), .in28(CSR_R), .out(Result), .sel(inst[6:2]));  // open: in1, in2, in3, in7, in9, in10, in11, in14, in15, in16, in17, in18, in19, in20, in21, in22, in23, in26, in29, in30, in31
  Multiplexer #(.enable("false"), .select(2), .width(6)) multiplexer_7 (
    .in0(6'b001100), .in1(6'b001101), .in2(6'b001110), .out(multiplexer_7_out),
    .sel(demultiplexer_2_out0[1:0]));  // open: in3
  Multiplexer #(.enable("false"), .width(6)) multiplexer_8 (
    .in0(6'b010011), .in1(6'b010100), .out(multiplexer_8_out), .sel(I[23]));
  Multiplexer #(.enable("false"), .select(3), .width(6)) multiplexer_9 (
    .in0(6'b001111), .in1(6'b010000), .in2(6'b010001), .in4(6'b010010), .in5(multiplexer_8_out),
    .in6(6'b010101), .in7(6'b010110), .out(multiplexer_9_out), .sel(demultiplexer_2_out1));  // open: in3
  not not_1 (not_1_out, inst[4]);
  and and_1 (and_1_out, not_1_out, inst[6]);
  Multiplexer #(.enable("false"), .width(6)) multiplexer_10 (
    .in0(multiplexer_7_out), .in1(multiplexer_9_out), .out(multiplexer_10_out), .sel(inst[4]));
  xor xor_1 (xor_1_out, inst[12], BrEq);
  not not_2 (not_2_out, inst[14]);
  xor xor_2 (xor_2_out, inst[12], BrLt);
  Multiplexer #(.enable("false"), .width(6)) multiplexer_11 (
    .in0(multiplexer_10_out), .in1(6'b100011), .out(I_R), .sel(inst[2]));
  and and_2 (and_2_out, xor_1_out, not_2_out);
  and and_3 (and_3_out, inst[14], xor_2_out);
  or or_3 (or_3_out, and_2_out, and_3_out);
  or or_4 (or_4_out, or_3_out, inst[2]);
  and and_4 (PCSel, or_4_out, and_1_out);

  // Other names for the same wires on the sheet: OP_CODE[4:0] = inst[6:2]

  // Notes on the sheet:
  //   INPUTS to circuit
  //   ROM Input  ->
  //   contents of rom_1 (hex, n*v repeats v):
  //   8004 8104 8184 8024 8124 8164 8044 8084 80a4 81a4 80c4 80e4 9200 9200 9200 9204 9224 9244 9284 92a4
  //   93a4 92c4 92e4 2210 2210 2210 4*3600 3e00 3e00 c604 c3e4 d608 9208 7201 7203
  //   ROM FOR CONTROL LOGIC
  //   DON'T CHANGE THE LOCATIONS OF THE INPUTS AND OUTPUTS!
  //   OUTPUT from circuit
  //   CLOSE
  //   WIRE
  //   TO
  //   USE
  //   ROM
  //   If 0th value = 1, chose 23
  //   Note: combinational logic for PCSel
endmodule
