// Logisim project cpu.circ as structural Verilog: 1 circuit, main circuit cpu
module cpu (
  input  clk,
  input  [31:0] INSTRUCTION,
  input  [31:0] MEM_READ_DATA,
  output [31:0] MEM_WRITE_ADDRESS,
  output [31:0] PROGRAM_COUNTER,
  output [31:0] ra,
  output [31:0] sp,
  output [31:0] t0,
  output [31:0] t1,
  output [31:0] t2,
  output [31:0] s0,
  output [31:0] s1,
  output [31:0] a0,
  output [31:0] tohost,
  output [3:0] MEM_WRITE_ENABLE,
  output [31:0] MEM_WRITE_DATA
);

  wire branch_comp_1_breq, branch_comp_1_brlt, control_logic_1_asel, control_logic_1_brun,
       control_logic_1_bsel, control_logic_1_csrsel, control_logic_1_csrwen, control_logic_1_memrw,
       control_logic_1_pcsel, control_logic_1_regwen;
  wire [1:0] control_logic_1_wbsel;
  wire [2:0] control_logic_1_immsel;
  wire [3:0] control_logic_1_alusel, multiplexer_10_out;
  wire [31:0] adder_1_out, bit_extender_1_out, bit_extender_2_out, bit_extender_3_out, bit_extender_4_out,
       bit_extender_5_out, bit_extender_6_out, imm_gen_1_imm, Instruct2, MEM_READ_Final, multiplexer_1_out,
       multiplexer_2_out, multiplexer_3_out, multiplexer_4_out, multiplexer_5_out, multiplexer_7_out, Read2,
       regfile_1_read_data_1, regfile_1_read_data_2, register_2_q, register_3_q;

  Adder #(.width(32)) adder_1 (.a(PROGRAM_COUNTER), .b(32'h4), .out(adder_1_out));  // open: cin, cout
  Multiplexer #(.enable("false"), .width(32)) multiplexer_1 (
    .in0(adder_1_out), .in1(MEM_WRITE_ADDRESS), .out(multiplexer_1_out), .sel(control_logic_1_pcsel));
  Multiplexer #(.enable("false"), .width(32)) multiplexer_2 (
    .in0(INSTRUCTION), .in1(32'h13), .out(multiplexer_2_out), .sel(control_logic_1_pcsel));
  Register #(.width(32)) PC (.D(multiplexer_1_out), .clk(clk), .Q(PROGRAM_COUNTER));  // open: en, clr
  Register #(.width(32)) register_1 (.D(multiplexer_2_out), .clk(clk), .Q(Instruct2));  // open: en, clr
  Register #(.width(32)) register_2 (.D(adder_1_out), .clk(clk), .Q(register_2_q));  // open: en, clr
  Register #(.width(32)) register_3 (.D(PROGRAM_COUNTER), .clk(clk), .Q(register_3_q));  // open: en, clr
  imm_gen imm_gen_1 (.inst(Instruct2), .ImmSel(control_logic_1_immsel), .imm(imm_gen_1_imm));
  control_logic control_logic_1 (
    .CSRWen(control_logic_1_csrwen), .PCSel(control_logic_1_pcsel), .RegWEn(control_logic_1_regwen),
    .ImmSel(control_logic_1_immsel), .BrUn(control_logic_1_brun), .ASel(control_logic_1_asel),
    .BSel(control_logic_1_bsel), .ALUSel(control_logic_1_alusel), .MemRW(control_logic_1_memrw),
    .WBSel(control_logic_1_wbsel), .CSRSel(control_logic_1_csrsel), .inst(Instruct2),
    .BrEq(branch_comp_1_breq), .BrLt(branch_comp_1_brlt));
  regfile regfile_1 (
    .rs1(Instruct2[19:15]), .rs2(Instruct2[24:20]), .rd(Instruct2[11:7]), .Write_Data(multiplexer_7_out),
    .RegWEn(control_logic_1_regwen), .clk(clk), .ra(ra), .sp(sp), .t0(t0), .t1(t1), .t2(t2), .s0(s0),
    .s1(s1), .a0(a0), .Read_Data_1(regfile_1_read_data_1), .Read_Data_2(regfile_1_read_data_2));
  branch_comp branch_comp_1 (
    .rs1(regfile_1_read_data_1), .rs2(regfile_1_read_data_2), .BrUn(control_logic_1_brun),
    .BrEq(branch_comp_1_breq), .BrLt(branch_comp_1_brlt));
  Multiplexer #(.enable("false"), .width(32)) multiplexer_3 (
    .in0(regfile_1_read_data_1), .in1(imm_gen_1_imm), .out(multiplexer_3_out), .sel(control_logic_1_csrsel));
  Multiplexer #(.enable("false"), .width(32)) multiplexer_4 (
    .in0(regfile_1_read_data_1), .in1(register_3_q), .out(multiplexer_4_out), .sel(control_logic_1_asel));
  Multiplexer #(.enable("false"), .width(32)) multiplexer_5 (
    .in0(regfile_1_read_data_2), .in1(imm_gen_1_imm), .out(multiplexer_5_out), .sel(control_logic_1_bsel));
  alu alu_1 (.Result(MEM_WRITE_ADDRESS), .A(multiplexer_4_out), .B(multiplexer_5_out), .ALUSel(control_logic_1_alusel));
  csr csr_1 (
    .CSR_address(Instruct2[31:20]), .CSR_din(multiplexer_3_out), .CSR_WE(control_logic_1_csrwen), .clk(clk),
    .tohost(tohost));
  Multiplexer #(.enable("false"), .width(32)) multiplexer_6 (
    .in0({32{1'b0}}), .in1(regfile_1_read_data_2), .out(Read2), .sel(control_logic_1_memrw));
  Multiplexer #(.enable("false"), .select(2), .width(32)) multiplexer_7 (
    .in0(MEM_READ_Final), .in1(MEM_WRITE_ADDRESS), .in2(register_2_q), .out(multiplexer_7_out),
    .sel(control_logic_1_wbsel));  // open: in3
  assign bit_extender_1_out = {{24{MEM_READ_DATA[7]}}, MEM_READ_DATA[7:0]};  // Bit_Extender bit_extender_1
  assign bit_extender_2_out = {{24{MEM_READ_DATA[15]}}, MEM_READ_DATA[15:8]};  // Bit_Extender bit_extender_2
  assign bit_extender_3_out = {{24{MEM_READ_DATA[23]}}, MEM_READ_DATA[23:16]};  // Bit_Extender bit_extender_3
  assign bit_extender_4_out = {{24{MEM_READ_DATA[31]}}, MEM_READ_DATA[31:24]};  // Bit_Extender bit_extender_4
  assign bit_extender_5_out = {{16{MEM_READ_DATA[15]}}, MEM_READ_DATA[15:0]};  // Bit_Extender bit_extender_5
  assign bit_extender_6_out = {{16{MEM_READ_DATA[31]}}, MEM_READ_DATA[31:16]};  // Bit_Extender bit_extender_6
  Multiplexer #(.enable("false"), .select(4), .width(32)) multiplexer_8 (
    .in0(bit_extender_1_out), .in1(bit_extender_2_out), .in2(bit_extender_3_out), .in3(bit_extender_4_out),
    .in4(bit_extender_5_out), .in6(bit_extender_6_out), .in8(MEM_READ_DATA), .out(MEM_READ_Final),
    .sel({Instruct2[13:12], MEM_WRITE_ADDRESS[1:0]}));  // open: in5, in7, in9, in10, in11, in12, in13, in14, in15
  Multiplexer #(.enable("false"), .select(4), .width(32)) multiplexer_9 (
    .in0({{24{1'b0}}, Read2[7:0]}), .in1({{16{1'b0}}, Read2[7:0], {8{1'b0}}}),
    .in2({{8{1'b0}}, Read2[7:0], {16{1'b0}}}), .in3({Read2[7:0], {24{1'b0}}}),
    .in4({{16{1'b0}}, Read2[15:0]}), .in6({Read2[15:0], {16{1'b0}}}), .in8(Read2), .out(MEM_WRITE_DATA),
    .sel({Instruct2[13:12], MEM_WRITE_ADDRESS[1:0]}));  // open: in5, in7, in9, in10, in11, in12, in13, in14, in15
  Multiplexer #(.enable("false"), .width(4)) multiplexer_10 (
    .in0(4'b1111), .in1({Instruct2[13:12], MEM_WRITE_ADDRESS[1:0]}), .out(multiplexer_10_out),
    .sel(control_logic_1_memrw));
  Multiplexer #(.enable("false"), .select(4), .width(4)) multiplexer_11 (
    .in0(4'b0001), .in1(4'b0010), .in2(4'b0100), .in3(4'b1000), .in4(4'b0011), .in6(4'b1100), .in8(4'b1111),
    .in15(4'b0000), .out(MEM_WRITE_ENABLE), .sel(multiplexer_10_out));  // open: in5, in7, in9, in10, in11, in12, in13, in14

  // Notes on the sheet:
  //   Output to IMEM
  //   PIPE3
  //   IMEM (do **NOT** move this)
  //   Inputs from IMEM
  //   PIPE 1
  //   FOR CSR (address)
  //   PIPE 2
  //   Inputs/Outputs for testing. Do **NOT** move these.
  //   Outputs To DMEM
  //   DMEM (do **NOT** move this)
  //   Inputs From DMEM
endmodule
