// Logisim project imm-gen.circ as structural Verilog: 1 circuit, main circuit imm_gen
module imm_gen (
  input  [31:0] inst,
  input  [2:0] ImmSel,
  output [31:0] imm
);

  wire [24:0] CSR, demultiplexer_1_out0, demultiplexer_1_out3, demultiplexer_1_out4, demultiplexer_1_out5,
       demultiplexer_1_out6, demultiplexer_1_out12, demultiplexer_1_out13, demultiplexer_1_out14,
       demultiplexer_1_out25, I, R, S, SB, U, UJ;
  wire [31:0] CSR_R, I_R, S_R, SB_R, UJ_R;

  Demultiplexer #(.enable("false"), .select(5), .width(25)) demultiplexer_1 (
    .out0(demultiplexer_1_out0), .out3(demultiplexer_1_out3), .out4(demultiplexer_1_out4),
    .out5(demultiplexer_1_out5), .out6(demultiplexer_1_out6), .out8(S), .out12(demultiplexer_1_out12),
    .out13(demultiplexer_1_out13), .out14(demultiplexer_1_out14), .out24(SB), .out25(demultiplexer_1_out25),
    .out27(UJ), .out28(CSR), .in(inst[31:7]), .sel(inst[6:2]));  // open: out1, out2, out7, out9, out10, out11, out15, out16, out17, out18, out19, out20, out21, out22, out23, out26, out29, out30, out31
  assign U = demultiplexer_1_out5 | demultiplexer_1_out13;  // OR_Gate or_1, 25 bits wide
  assign I_R = {{20{I[24]}}, I[24:13]};  // Bit_Extender bit_extender_1
  assign S_R = {{20{S[24]}}, {S[24:18], S[4:0]}};  // Bit_Extender bit_extender_2
  assign SB_R = {{19{SB[24]}}, {SB[24], SB[0], SB[23:18], SB[4:1], 1'b0}};  // Bit_Extender bit_extender_3
  assign I = demultiplexer_1_out0 | demultiplexer_1_out3 | demultiplexer_1_out4 | demultiplexer_1_out6 | demultiplexer_1_out25;  // OR_Gate or_2, 25 bits wide
  assign R = demultiplexer_1_out12 | demultiplexer_1_out14;  // OR_Gate or_3, 25 bits wide
  assign UJ_R = {{11{UJ[24]}}, {UJ[24], UJ[12:5], UJ[13], UJ[23:14], 1'b0}};  // Bit_Extender bit_extender_4
  assign CSR_R = {{27{1'b0}}, CSR[12:8]};  // Bit_Extender bit_extender_5
  Multiplexer #(.enable("false"), .select(5), .width(32)) multiplexer_1 (
    .in0(I_R), .in3(I_R), .in4(I_R), .in5({U[24:5], {12{1'b0}}}), .in6(I_R), .in8(S_R),
    .in13({U[24:5], {12{1'b0}}}), .in24(SB_R), .in25(I_R), .in27(UJ_R), .in28(CSR_R), .out(imm),
    .sel(inst[6:2]));  // open: in1, in2, in7, in9, in10, in11, in12, in14, in15, in16, in17, in18, in19, in20, in21, in22, in23, in26, in29, in30, in31

  // Other names for the same wires on the sheet: U_R[31:12] = U[24:5]

  // Notes on the sheet:
  //   INPUTS to circuit
  //   Could probably do something with MUX (OPcode as selector) to check
  //   DON'T CHANGE THE LOCATIONS OF THE INPUTS AND OUTPUTS!
  //   OUTPUT from circuit
endmodule
