// Logisim project regfile.circ as structural Verilog: 1 circuit, main circuit regfile
module regfile (
  input  [4:0] rs1,
  input  [4:0] rs2,
  input  [4:0] rd,
  input  [31:0] Write_Data,
  input  RegWEn,
  input  clk,
  output [31:0] ra,
  output [31:0] sp,
  output [31:0] t0,
  output [31:0] t1,
  output [31:0] t2,
  output [31:0] s0,
  output [31:0] s1,
  output [31:0] a0,
  output [31:0] Read_Data_1,
  output [31:0] Read_Data_2
);

  wire clk3, d_ff_1_q, nope, write_en1, write_en2, write_en3, write_en4, write_en5, write_en6, write_en7,
       write_en8, write_en9, write_en10, write_en11, write_en12, write_en13, write_en14, write_en15,
       write_en16, write_en17, write_en18, write_en19, write_en20, write_en21, write_en22, write_en23,
       write_en24, write_en25, write_en26, write_en27, write_en28, write_en29, write_en30, write_en31;
  wire [31:0] a0P, multiplexer_2_out, multiplexer_3_out, multiplexer_4_out, multiplexer_5_out,
       multiplexer_6_out, multiplexer_7_out, multiplexer_8_out, multiplexer_9_out, multiplexer_11_out,
       multiplexer_12_out, multiplexer_13_out, multiplexer_14_out, multiplexer_15_out, multiplexer_16_out,
       multiplexer_17_out, multiplexer_18_out, multiplexer_19_out, multiplexer_20_out, multiplexer_21_out,
       multiplexer_22_out, multiplexer_23_out, multiplexer_24_out, multiplexer_25_out, multiplexer_26_out,
       multiplexer_27_out, multiplexer_28_out, multiplexer_29_out, multiplexer_30_out, multiplexer_31_out,
       multiplexer_32_out, multiplexer_33_out, noop, obsolete, Px11, Px12, Px13, Px14, Px15, Px16, Px17,
       Px18, Px19, Px20, Px21, Px22, Px23, Px24, Px25, Px26, Px27, Px28, Px29, Px30, Px31, raP, s0P, s1P,
       spP, t0P, t1P, t2P, x3, x3P, x4, x4P, x11, x12, x13, x14, x15, x16, x17, x18, x19, x20, x21, x22, x23,
       x24, x25, x26, x27, x28, x29, x30, x31;

  Demultiplexer #(.enable("false"), .select(5), .width(32)) demultiplexer_1 (
    .out1(raP), .out2(spP), .out3(x3P), .out4(x4P), .out5(t0P), .out6(t1P), .out7(t2P), .out8(s0P),
    .out9(s1P), .out10(a0P), .out11(Px11), .out12(Px12), .out13(Px13), .out14(Px14), .out15(Px15),
    .out16(Px16), .out17(Px17), .out18(Px18), .out19(Px19), .out20(Px20), .out21(Px21), .out22(Px22),
    .out23(Px23), .out24(Px24), .out25(Px25), .out26(Px26), .out27(Px27), .out28(Px28), .out29(Px29),
    .out30(Px30), .out31(Px31), .in(Write_Data), .sel(rd));  // open: out0
  Demultiplexer #(.enable("false"), .select(5)) demultiplexer_2 (
    .out1(write_en1), .out2(write_en2), .out3(write_en3), .out4(write_en4), .out5(write_en5),
    .out6(write_en6), .out7(write_en7), .out8(write_en8), .out9(write_en9), .out10(write_en10),
    .out11(write_en11), .out12(write_en12), .out13(write_en13), .out14(write_en14), .out15(write_en15),
    .out16(write_en16), .out17(write_en17), .out18(write_en18), .out19(write_en19), .out20(write_en20),
    .out21(write_en21), .out22(write_en22), .out23(write_en23), .out24(write_en24), .out25(write_en25),
    .out26(write_en26), .out27(write_en27), .out28(write_en28), .out29(write_en29), .out30(write_en30),
    .out31(write_en31), .in(RegWEn), .sel(rd));  // open: out0
  Multiplexer #(.enable("false"), .select(5), .width(32)) multiplexer_1 (
    .in0({32{1'b0}}), .in1(ra), .in2(sp), .in3(x3), .in4(x4), .in5(t0), .in6(t1), .in7(t2), .in8(s0),
    .in9(s1), .in10(a0), .in11(x11), .in12(x12), .in13(x13), .in14(x14), .in15(x15), .in16(x16), .in17(x17),
    .in18(x18), .in19(x19), .in20(x20), .in21(x21), .in22(x22), .in23(x23), .in24(x24), .in25(x25),
    .in26(x26), .in27(x27), .in28(x28), .in29(x29), .in30(x30), .in31(x31), .out(Read_Data_1), .sel(rs1));
  Register #(.width(32)) register_1 (.D(multiplexer_2_out), .en(write_en1), .clk(clk), .Q(ra));  // open: clr
  Multiplexer #(.enable("false"), .width(32)) multiplexer_2 (
    .in0(ra), .in1(raP), .out(multiplexer_2_out), .sel(write_en1));
  Register #(.width(32)) register_2 (.D(multiplexer_3_out), .en(write_en5), .clk(clk), .Q(t0));  // open: clr
  Multiplexer #(.enable("false"), .width(32)) multiplexer_3 (
    .in0(t0), .in1(t0P), .out(multiplexer_3_out), .sel(write_en5));
  Register #(.width(32)) register_3 (.D(multiplexer_4_out), .en(write_en9), .clk(clk), .Q(s1));  // open: clr
  Multiplexer #(.enable("false"), .width(32)) multiplexer_4 (
    .in0(s1), .in1(s1P), .out(multiplexer_4_out), .sel(write_en9));
  Register #(.width(32)) register_4 (.D(multiplexer_5_out), .en(write_en13), .clk(clk), .Q(x13));  // open: clr
  Multiplexer #(.enable("false"), .width(32)) multiplexer_5 (
    .in0(x13), .in1(Px13), .out(multiplexer_5_out), .sel(write_en13));
  Register #(.width(32)) register_5 (.D(multiplexer_6_out), .en(write_en17), .clk(clk), .Q(x17));  // open: clr
  Multiplexer #(.enable("false"), .width(32)) multiplexer_6 (
    .in0(x17), .in1(Px17), .out(multiplexer_6_out), .sel(write_en17));
  Register #(.width(32)) register_6 (.D(multiplexer_7_out), .en(write_en21), .clk(clk), .Q(x21));  // open: clr
  Multiplexer #(.enable("false"), .width(32)) multiplexer_7 (
    .in0(x21), .in1(Px21), .out(multiplexer_7_out), .sel(write_en21));
  Register #(.width(32)) register_7 (.D(multiplexer_8_out), .en(write_en25), .clk(clk), .Q(x25));  // open: clr
  Multiplexer #(.enable("false"), .width(32)) multiplexer_8 (
    .in0(x25), .in1(Px25), .out(multiplexer_8_out), .sel(write_en25));
  Register #(.width(32)) register_8 (.D(multiplexer_9_out), .en(write_en29), .clk(clk), .Q(x29));  // open: clr
  Multiplexer #(.enable("false"), .width(32)) multiplexer_9 (
    .in0(x29), .in1(Px29), .out(multiplexer_9_out), .sel(write_en29));
  Multiplexer #(.enable("false"), .select(5), .width(32)) multiplexer_10 (
    .in0({32{1'b0}}), .in1(ra), .in2(sp), .in3(x3), .in4(x4), .in5(t0), .in6(t1), .in7(t2), .in8(s0),
    .in9(s1), .in10(a0), .in11(x11), .in12(x12), .in13(x13), .in14(x14), .in15(x15), .in16(x16), .in17(x17),
    .in18(x18), .in19(x19), .in20(x20), .in21(x21), .in22(x22), .in23(x23), .in24(x24), .in25(x25),
    .in26(x26), .in27(x27), .in28(x28), .in29(x29), .in30(x30), .in31(x31), .out(Read_Data_2), .sel(rs2));
  Register #(.width(32)) register_9 (.D(multiplexer_11_out), .en(write_en2), .clk(clk), .Q(sp));  // open: clr
  Multiplexer #(.enable("false"), .width(32)) multiplexer_11 (
    .in0(sp), .in1(spP), .out(multiplexer_11_out), .sel(write_en2));
  Register #(.width(32)) register_10 (.D(multiplexer_12_out), .en(write_en6), .clk(clk), .Q(t1));  // open: clr
  Multiplexer #(.enable("false"), .width(32)) multiplexer_12 (
    .in0(t1), .in1(t1P), .out(multiplexer_12_out), .sel(write_en6));
  Register #(.width(32)) register_11 (.D(multiplexer_13_out), .en(write_en10), .clk(clk), .Q(a0));  // open: clr
  Multiplexer #(.enable("false"), .width(32)) multiplexer_13 (
    .in0(a0), .in1(a0P), .out(multiplexer_13_out), .sel(write_en10));
  Register #(.width(32)) register_12 (.D(multiplexer_14_out), .en(write_en14), .clk(clk), .Q(x14));  // open: clr
  Multiplexer #(.enable("false"), .width(32)) multiplexer_14 (
    .in0(x14), .in1(Px14), .out(multiplexer_14_out), .sel(write_en14));
  Register #(.width(32)) register_13 (.D(multiplexer_15_out), .en(write_en18), .clk(clk), .Q(x18));  // open: clr
  Multiplexer #(.enable("false"), .width(32)) multiplexer_15 (
    .in0(x18), .in1(Px18), .out(multiplexer_15_out), .sel(write_en18));
  Register #(.width(32)) register_14 (.D(multiplexer_16_out), .en(write_en22), .clk(clk), .Q(x22));  // open: clr
  Multiplexer #(.enable("false"), .width(32)) multiplexer_16 (
    .in0(x22), .in1(Px22), .out(multiplexer_16_out), .sel(write_en22));
  Register #(.width(32)) register_15 (.D(multiplexer_17_out), .en(write_en26), .clk(clk), .Q(x26));  // open: clr
  Multiplexer #(.enable("false"), .width(32)) multiplexer_17 (
    .in0(x26), .in1(Px26), .out(multiplexer_17_out), .sel(write_en26));
  Register #(.width(32)) register_16 (.D(multiplexer_18_out), .en(write_en30), .clk(clk), .Q(x30));  // open: clr
  Multiplexer #(.enable("false"), .width(32)) multiplexer_18 (
    .in0(x30), .in1(Px30), .out(multiplexer_18_out), .sel(write_en30));
  Register #(.width(32)) register_17 (.D(multiplexer_19_out), .en(write_en3), .clk(clk), .Q(x3));  // open: clr
  Multiplexer #(.enable("false"), .width(32)) multiplexer_19 (
    .in0(x3), .in1(x3P), .out(multiplexer_19_out), .sel(write_en3));
  Register #(.width(32)) register_18 (.D(multiplexer_20_out), .en(write_en7), .clk(clk), .Q(t2));  // open: clr
  Multiplexer #(.enable("false"), .width(32)) multiplexer_20 (
    .in0(t2), .in1(t2P), .out(multiplexer_20_out), .sel(write_en7));
  Register #(.width(32)) register_19 (.D(multiplexer_21_out), .en(write_en11), .clk(clk), .Q(x11));  // open: clr
  Multiplexer #(.enable("false"), .width(32)) multiplexer_21 (
    .in0(x11), .in1(Px11), .out(multiplexer_21_out), .sel(write_en11));
  Register #(.width(32)) register_20 (.D(multiplexer_22_out), .en(write_en15), .clk(clk), .Q(x15));  // open: clr
  Multiplexer #(.enable("false"), .width(32)) multiplexer_22 (
    .in0(x15), .in1(Px15), .out(multiplexer_22_out), .sel(write_en15));
  Register #(.width(32)) register_21 (.D(multiplexer_23_out), .en(write_en19), .clk(clk), .Q(x19));  // open: clr
  Multiplexer #(.enable("false"), .width(32)) multiplexer_23 (
    .in0(x19), .in1(Px19), .out(multiplexer_23_out), .sel(write_en19));
  Register #(.width(32)) register_22 (.D(multiplexer_24_out), .en(write_en23), .clk(clk), .Q(x23));  // open: clr
  Multiplexer #(.enable("false"), .width(32)) multiplexer_24 (
    .in0(x23), .in1(Px23), .out(multiplexer_24_out), .sel(write_en23));
  Register #(.width(32)) register_23 (.D(multiplexer_25_out), .en(write_en27), .clk(clk), .Q(x27));  // open: clr
  Multiplexer #(.enable("false"), .width(32)) multiplexer_25 (
    .in0(x27), .in1(Px27), .out(multiplexer_25_out), .sel(write_en27));
  Register #(.width(32)) register_24 (.D(multiplexer_26_out), .en(write_en31), .clk(clk), .Q(x31));  // open: clr
  Multiplexer #(.enable("false"), .width(32)) multiplexer_26 (
    .in0(x31), .in1(Px31), .out(multiplexer_26_out), .sel(write_en31));
  D_Flip_Flop d_ff_1 (.D(nope), .clk(clk3), .Q(d_ff_1_q));  // open: Qn, preset, reset
  Register #(.width(32)) register_25 (.D(noop), .en(d_ff_1_q), .clk(clk3), .Q(obsolete));  // open: clr
  Register #(.width(32)) register_26 (.D(multiplexer_27_out), .en(write_en4), .clk(clk), .Q(x4));  // open: clr
  Multiplexer #(.enable("false"), .width(32)) multiplexer_27 (
    .in0(x4), .in1(x4P), .out(multiplexer_27_out), .sel(write_en4));
  Register #(.width(32)) register_27 (.D(multiplexer_28_out), .en(write_en8), .clk(clk), .Q(s0));  // open: clr
  Multiplexer #(.enable("false"), .width(32)) multiplexer_28 (
    .in0(s0), .in1(s0P), .out(multiplexer_28_out), .sel(write_en8));
  Register #(.width(32)) register_28 (.D(multiplexer_29_out), .en(write_en12), .clk(clk), .Q(x12));  // open: clr
  Multiplexer #(.enable("false"), .width(32)) multiplexer_29 (
    .in0(x12), .in1(Px12), .out(multiplexer_29_out), .sel(write_en12));
  Register #(.width(32)) register_29 (.D(multiplexer_30_out), .en(write_en16), .clk(clk), .Q(x16));  // open: clr
  Multiplexer #(.enable("false"), .width(32)) multiplexer_30 (
    .in0(x16), .in1(Px16), .out(multiplexer_30_out), .sel(write_en16));
  Register #(.width(32)) register_30 (.D(multiplexer_31_out), .en(write_en20), .clk(clk), .Q(x20));  // open: clr
  Multiplexer #(.enable("false"), .width(32)) multiplexer_31 (
    .in0(x20), .in1(Px20), .out(multiplexer_31_out), .sel(write_en20));
  Register #(.width(32)) register_31 (.D(multiplexer_32_out), .en(write_en24), .clk(clk), .Q(x24));  // open: clr
  Multiplexer #(.enable("false"), .width(32)) multiplexer_32 (
    .in0(x24), .in1(Px24), .out(multiplexer_32_out), .sel(write_en24));
  Register #(.width(32)) register_32 (.D(multiplexer_33_out), .en(write_en28), .clk(clk), .Q(x28));  // open: clr
  Multiplexer #(.enable("false"), .width(32)) multiplexer_33 (
    .in0(x28), .in1(Px28), .out(multiplexer_33_out), .sel(write_en28));

  // Other names for the same wires on the sheet: read_data1[31:0] = Read_Data_1; read_data2[31:0] = Read_Data_2;
  //   read_reg1[4:0] = rs1; read_reg2[4:0] = rs2; write_en = RegWEn; write_reg[4:0] = rd

  // Notes on the sheet:
  //   INPUTS to circuit
  //   DON'T CHANGE THE LOCATIONS OF THE INPUTS AND OUTPUTS!
  //   DEBUG/TEST purpose output
  //   OUTPUTS from circuit
endmodule
